# Fritzing sketch basic-setup (saved by Fritzing 0.9.10b)
breadboards: 1

parts:
  Teensy1 = Teensy 2.0
  R1 = Resistor [tolerance=±5% resistance=100k package="1206 [SMD]"]
  Part1 = 16 NeoPixel Ring [part_number=1463]

nets:
  GND: Teensy1.GND, Part1.GND
  N1: Teensy1.B2, Part1.IN
  VCC: Teensy1.VCC, Part1.VDD
  N2: Teensy1.F4, R1.Pin_0
  N3: Teensy1.F0, R1.Pin_1

custom parts:
  16 NeoPixel Ring: 16 ultra bright smart LED NeoPixels are arranged in a circle with 1.75" (44.5mm) outer diameter. The rings are 'chainable' - connect the output pin of one to the input pin of another. Use only one microcontroller pin to control as many as you can chain together! Each LED is addressable as the driver chip is inside the LED. Each one has ~18mA constant current drive so the color will be very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
